# Fritzing sketch Diagrama de conexiones (saved by Fritzing 0.9.10b)
breadboards: 1

parts:
  Mod1 = Raspberry Pi 4B
  HC-SR04_Sensor_1 = HC-SR04 Ultrasonic Distance Sensor
  M2 = DC Motor [voltage_(max)=6V voltage_(min)=3V]
  S1 = H-Bridge with L298N
  BAT1 = BC9VPC [package=bc9vpc]
  M1 = fc-51 [package=THT]
  M3 = fc-51 [package=THT]

nets:
  5V: Mod1.5V, HC-SR04_Sensor_1.VCC, S1.ENA-5V, M1.pin3, M3.pin3
  GND: Mod1.GND, HC-SR04_Sensor_1.GND, S1.ENA, M1.pin2, M3.pin2
  N1: Mod1.GPIO17, HC-SR04_Sensor_1.TRIG
  N2: Mod1.GPIO27, HC-SR04_Sensor_1.ECHO
  N3: Mod1.GPIO22, M1.pin1
  N4: Mod1.GPIO24, M3.pin1
  N5: Mod1.GPIO20, S1.IN3
  N6: Mod1.GPIO21, S1.IN4
  N7: M2.pin_1, S1.M2-02
  N8: M2.pin_2, S1.M1-02, S1.M2-01
  N9: S1.12V, BAT1.V+
  N10: S1.GND, BAT1.V-

custom parts:
  H-Bridge with L298N: h-bridge
